// Logisim project MIPSProcessor.circ as structural Verilog
module MIPS32 (
);

  wire clock_1_out, exmem_1_lbout, exmem_1_lbuout, exmem_1_lwout, exmem_1_sbout, exmem_1_skipout,
       exmem_1_swout, hazards_1_stall, idex_1_idexmro, idex_1_iout, idex_1_lbout, idex_1_lbuout,
       idex_1_luiout, idex_1_lwout, idex_1_movnout, idex_1_movzout, idex_1_sbout, idex_1_sltiout,
       idex_1_sltiuout, idex_1_sltout, idex_1_sltuout, idex_1_svarout, idex_1_swout, idex_1_wdisout,
       inexecute_1_lbout, inexecute_1_lbuout, inexecute_1_load, inexecute_1_lwout, inexecute_1_sbout,
       inexecute_1_swout, inexecute_1_wdis, inexecute_1_zap, inmemory_1_wdis, instrcutionwriteback_1_we,
       instructiondecode_1_i, instructiondecode_1_idexmemr, instructiondecode_1_lb, instructiondecode_1_lbu,
       instructiondecode_1_lui, instructiondecode_1_lw, instructiondecode_1_movn, instructiondecode_1_movz,
       instructiondecode_1_sb, instructiondecode_1_shiftvar, instructiondecode_1_skipout,
       instructiondecode_1_slt, instructiondecode_1_slti, instructiondecode_1_sltiu,
       instructiondecode_1_sltu, instructiondecode_1_sw, memwb_1_skipout, not_1_out, not_2_out;
  wire [1:0] hazards_1_hazarda, hazards_1_hazardb;
  wire [2:0] idex_1_jout, instructiondecode_1_jump;
  wire [3:0] idex_1_branout, idex_1_ctrlout, instructiondecode_1_branch, instructiondecode_1_ctrl;
  wire [4:0] exmem_1_rdout, exmem_1_rtout, idex_1_rdout, idex_1_rsout, idex_1_rtout, idex_1_saout,
       ifid_1_ifidrs, ifid_1_ifidrt, inexecute_1_rdout, inexecute_1_rtout, inmemory_1_wdest,
       instrcutionwriteback_1_rdout, instructiondecode_1_rdout, instructiondecode_1_rsout,
       instructiondecode_1_rtout, instructiondecode_1_sa, instructionfetch_1_idrs, instructionfetch_1_ifrt,
       memwb_1_rdout;
  wire [31:0] exmem_1_adrout, exmem_1_aout, exmem_1_dout, exmem_1_rtvout, idex_1_aout, idex_1_bout,
       idex_1_immout, idex_1_injout, idex_1_offout, idex_1_plus4out, ifid_1_instout, ifid_1_pcplus4out,
       inexecute_1_aout, inexecute_1_d, inexecute_1_memadr, inexecute_1_rtval, inexecute_1_taddress,
       inmemory_1_aout, inmemory_1_dout, instrcutionwriteback_1_result, instructiondecode_1_a,
       instructiondecode_1_b, instructiondecode_1_imm, instructiondecode_1_indexj,
       instructiondecode_1_manipoff, instructiondecode_1_pcplus4out, instructionfetch_1_inst,
       instructionfetch_1_pcplus4, memwb_1_dout, multiplexer_1_out, multiplexer_2_out, multiplexer_3_out,
       multiplexer_4_out;

  Clock clock_1 (.out(clock_1_out));
  instructionFetch instructionfetch_1 (
    .clck(clock_1_out), .zap(inexecute_1_zap), .TAddress(inexecute_1_taddress), .Stall(hazards_1_stall),
    .inst(instructionfetch_1_inst), .PCPlus4(instructionfetch_1_pcplus4), .IFrt(instructionfetch_1_ifrt),
    .IDrs(instructionfetch_1_idrs));
  IFID ifid_1 (
    .inst(instructionfetch_1_inst), .PCPlus4(instructionfetch_1_pcplus4), .clck(clock_1_out),
    .IFrt(instructionfetch_1_ifrt), .IFrs(instructionfetch_1_idrs), .Stall(hazards_1_stall),
    .instOut(ifid_1_instout), .PCPlus4Out(ifid_1_pcplus4out), .IFIDrt(ifid_1_ifidrt), .IFIDrs(ifid_1_ifidrs));
  instructionDecode instructiondecode_1 (
    .D(instrcutionwriteback_1_result), .skip(instrcutionwriteback_1_we), .clck(clock_1_out),
    .inst(ifid_1_instout), .PCPlus4(ifid_1_pcplus4out), .rd(instrcutionwriteback_1_rdout),
    .A(instructiondecode_1_a), .B(instructiondecode_1_b), .rdOut(instructiondecode_1_rdout),
    .Sa(instructiondecode_1_sa), .imm(instructiondecode_1_imm), .SLTIU(instructiondecode_1_sltiu),
    .ctrl(instructiondecode_1_ctrl), .SLTI(instructiondecode_1_slti), .I(instructiondecode_1_i),
    .SLTU(instructiondecode_1_sltu), .SLT(instructiondecode_1_slt), .skipOut(instructiondecode_1_skipout),
    .LUI(instructiondecode_1_lui), .MOVN(instructiondecode_1_movn), .MOVZ(instructiondecode_1_movz),
    .PCPlus4out(instructiondecode_1_pcplus4out), .rtOut(instructiondecode_1_rtout),
    .rsOut(instructiondecode_1_rsout), .shiftVar(instructiondecode_1_shiftvar),
    .indexJ(instructiondecode_1_indexj), .manipOff(instructiondecode_1_manipoff),
    .JUMP(instructiondecode_1_jump), .Branch(instructiondecode_1_branch), .LW(instructiondecode_1_lw),
    .LB(instructiondecode_1_lb), .LBU(instructiondecode_1_lbu), .SW(instructiondecode_1_sw),
    .IDEXMEMR(instructiondecode_1_idexmemr), .SB(instructiondecode_1_sb));
  not not_1 (not_1_out, memwb_1_skipout);
  IDEX idex_1 (
    .A(instructiondecode_1_a), .B(instructiondecode_1_b), .Sa(instructiondecode_1_sa),
    .imm(instructiondecode_1_imm), .SLTIU(instructiondecode_1_sltiu), .ctrl(instructiondecode_1_ctrl),
    .SLTI(instructiondecode_1_slti), .I(instructiondecode_1_i), .clck(clock_1_out),
    .SLTU(instructiondecode_1_sltu), .SLT(instructiondecode_1_slt), .Wdis(instructiondecode_1_skipout),
    .LUI(instructiondecode_1_lui), .MOVN(instructiondecode_1_movn), .MOVZ(instructiondecode_1_movz),
    .PCPlus4(instructiondecode_1_pcplus4out), .rd(instructiondecode_1_rdout), .rt(instructiondecode_1_rtout),
    .rs(instructiondecode_1_rsout), .shiftVar(instructiondecode_1_shiftvar),
    .indexJ(instructiondecode_1_indexj), .manipOff(instructiondecode_1_manipoff),
    .JUMP(instructiondecode_1_jump), .Branch(instructiondecode_1_branch), .LW(instructiondecode_1_lw),
    .LB(instructiondecode_1_lb), .LBU(instructiondecode_1_lbu), .SW(instructiondecode_1_sw),
    .IDEXMEMR(instructiondecode_1_idexmemr), .stall(hazards_1_stall), .SB(instructiondecode_1_sb),
    .Aout(idex_1_aout), .Bout(idex_1_bout), .SaOut(idex_1_saout), .immOut(idex_1_immout),
    .SLTIUout(idex_1_sltiuout), .ctrlOut(idex_1_ctrlout), .SLTIout(idex_1_sltiout), .Iout(idex_1_iout),
    .SLTUout(idex_1_sltuout), .SLTout(idex_1_sltout), .WdisOut(idex_1_wdisout), .LUIout(idex_1_luiout),
    .MOVNout(idex_1_movnout), .MOVZout(idex_1_movzout), .rdOut(idex_1_rdout), .rtOut(idex_1_rtout),
    .rsOut(idex_1_rsout), .SVarOut(idex_1_svarout), .inJOut(idex_1_injout), .offOut(idex_1_offout),
    .Jout(idex_1_jout), .branOut(idex_1_branout), .plus4out(idex_1_plus4out), .LWOut(idex_1_lwout),
    .LBOut(idex_1_lbout), .LBUOut(idex_1_lbuout), .SWOut(idex_1_swout), .IDEXMRO(idex_1_idexmro),
    .SBOut(idex_1_sbout));
  not not_2 (not_2_out, exmem_1_skipout);
  InExecute inexecute_1 (
    .A(multiplexer_3_out), .B(multiplexer_1_out), .Sa(idex_1_saout), .imm(idex_1_immout),
    .SLTIU(idex_1_sltiuout), .ctrl(idex_1_ctrlout), .SLTI(idex_1_sltiout), .I(idex_1_iout),
    .SLTU(idex_1_sltuout), .SLT(idex_1_sltout), .skip(idex_1_wdisout), .LUI(idex_1_luiout),
    .MOVN(idex_1_movnout), .MOVZ(idex_1_movzout), .rd(idex_1_rdout), .shiftVar(idex_1_svarout),
    .indexJ(idex_1_injout), .manipOff(idex_1_offout), .jump(idex_1_jout), .Branch(idex_1_branout),
    .PCPlus4(idex_1_plus4out), .LW(idex_1_lwout), .LB(idex_1_lbout), .LBU(idex_1_lbuout), .SW(idex_1_swout),
    .rt(idex_1_rtout), .SB(idex_1_sbout), .Aout(inexecute_1_aout), .D(inexecute_1_d),
    .Wdis(inexecute_1_wdis), .rdOut(inexecute_1_rdout), .TAddress(inexecute_1_taddress),
    .zap(inexecute_1_zap), .MEMAdr(inexecute_1_memadr), .rtVal(inexecute_1_rtval), .LWOut(inexecute_1_lwout),
    .LBOut(inexecute_1_lbout), .LBUOut(inexecute_1_lbuout), .SWOut(inexecute_1_swout),
    .rtOut(inexecute_1_rtout), .SBOut(inexecute_1_sbout), .LOAD(inexecute_1_load));
  Hazards hazards_1 (
    .IDEXrt(idex_1_rtout), .IDEXrs(idex_1_rsout), .EXMEMrd(exmem_1_rdout), .EXMEMregWrite(not_2_out),
    .MEMWBrd(memwb_1_rdout), .MEMWBregWrite(not_1_out), .IDEXMemread(idex_1_idexmro), .IFIDrs(ifid_1_ifidrs),
    .IFIDrt(ifid_1_ifidrt), .LOAD(inexecute_1_load), .HazardA(hazards_1_hazarda),
    .HazardB(hazards_1_hazardb), .Stall(hazards_1_stall));
  EXMEM exmem_1 (
    .A(inexecute_1_aout), .D(inexecute_1_d), .clck(clock_1_out), .skip(inexecute_1_wdis),
    .rd(inexecute_1_rdout), .MemAdr(inexecute_1_memadr), .rtVal(inexecute_1_rtval), .LW(inexecute_1_lwout),
    .LB(inexecute_1_lbout), .LBU(inexecute_1_lbuout), .Sw(inexecute_1_swout), .rt(inexecute_1_rtout),
    .SB(inexecute_1_sbout), .Aout(exmem_1_aout), .Dout(exmem_1_dout), .skipOut(exmem_1_skipout),
    .rdOut(exmem_1_rdout), .AdrOut(exmem_1_adrout), .rtVOut(exmem_1_rtvout), .LWOut(exmem_1_lwout),
    .LBOut(exmem_1_lbout), .LBUOut(exmem_1_lbuout), .SWOut(exmem_1_swout), .rtOut(exmem_1_rtout),
    .SBOut(exmem_1_sbout));
  Multiplexer #(.width(32), .enable("false")) multiplexer_1 (
    .in0(multiplexer_2_out), .in1(exmem_1_dout), .out(multiplexer_1_out), .sel(hazards_1_hazardb[1]));
  inMemory inmemory_1 (
    .A(exmem_1_aout), .D(exmem_1_dout), .skip(exmem_1_skipout), .rd(exmem_1_rdout), .MemAdr(exmem_1_adrout),
    .rtVal(exmem_1_rtvout), .LW(exmem_1_lwout), .LB(exmem_1_lbout), .LBU(exmem_1_lbuout), .SW(exmem_1_swout),
    .rt(exmem_1_rtout), .clck(clock_1_out), .SB(exmem_1_sbout), .Aout(inmemory_1_aout),
    .Dout(inmemory_1_dout), .Wdis(inmemory_1_wdis), .Wdest(inmemory_1_wdest));
  Multiplexer #(.width(32), .enable("false")) multiplexer_2 (
    .in0(idex_1_bout), .in1(memwb_1_dout), .out(multiplexer_2_out), .sel(hazards_1_hazardb[0]));
  Multiplexer #(.width(32), .enable("false")) multiplexer_3 (
    .in0(multiplexer_4_out), .in1(exmem_1_dout), .out(multiplexer_3_out), .sel(hazards_1_hazarda[1]));
  MEMWB memwb_1 (
    .A(inmemory_1_aout), .D(inmemory_1_dout), .clck(clock_1_out), .skip(inmemory_1_wdis),
    .rd(inmemory_1_wdest), .Dout(memwb_1_dout), .skipOut(memwb_1_skipout), .rdOut(memwb_1_rdout));
  Multiplexer #(.width(32), .enable("false")) multiplexer_4 (
    .in0(idex_1_aout), .in1(memwb_1_dout), .out(multiplexer_4_out), .sel(hazards_1_hazarda[0]));
  instrcutionWriteback instrcutionwriteback_1 (
    .D(memwb_1_dout), .rd(memwb_1_rdout), .skip(memwb_1_skipout), .result(instrcutionwriteback_1_result),
    .rdOut(instrcutionwriteback_1_rdout), .WE(instrcutionwriteback_1_we));
endmodule

module instructionFetch (
  input  clck,
  input  zap,
  input  [31:0] TAddress,
  input  Stall,
  output [31:0] inst,
  output [31:0] PCPlus4,
  output [4:0] IFrt,
  output [4:0] IDrs
);

  wire incrementer_1_p1, not_1_out;
  wire [31:0] and_1_out, bit_extender_1_out, mipsprogramrom_1_p2, multiplexer_1_out, multiplexer_2_out;
  wire [31:2] register_1_q;

  Register #(.width(32)) register_1 (
    .D(multiplexer_1_out), .en(incrementer_1_p1), .clk(clck), .Q({register_1_q, PCPlus4[1:0]}));  // open: clr
  Multiplexer #(.width(32), .enable("false")) multiplexer_1 (
    .in0(multiplexer_2_out), .in1({register_1_q, PCPlus4[1:0]}), .out(multiplexer_1_out), .sel(Stall));
  Multiplexer #(.width(32), .enable("false")) multiplexer_2 (
    .in0(PCPlus4), .in1(TAddress), .out(multiplexer_2_out), .sel(zap));
  // Incrementer #(.width(30)) incrementer_1: pin names not known; wires that end beside it: incrementer_1_p1, register_1_q, PCPlus4[31:2]
  not not_1 (not_1_out, zap);
  // MIPSProgramROM mipsprogramrom_1: pin names not known; wires that end beside it: {register_1_q, PCPlus4[1:0]}, mipsprogramrom_1_p2
  assign bit_extender_1_out = {{31{not_1_out}}, not_1_out};  // Bit_Extender bit_extender_1
  assign and_1_out = bit_extender_1_out & TAddress;  // AND_Gate and_1, 32 bits wide
  Multiplexer #(.width(32), .enable("false")) multiplexer_3 (
    .in0(mipsprogramrom_1_p2), .in1(and_1_out), .out({inst[31:26], IDrs, IFrt, inst[15:0]}), .sel(zap));

  assign inst[25:16] = {IDrs, IFrt};

  // Notes on the sheet:
  //   contents of mipsprogramrom_1 (hex, n*v repeats v):
  //   #Table B tests  #Jump Test Cases  #J Test cases:  J num1 #jumping forard SLL $0, $0, 0 ADDIU $1,
  //   $zero, 5 #should be flushed ADDIU $2, $zero, 6 #should not be executed so $2 should stay 0 num2:
  //   ADDIU $6, $zero, 1 # register 6 should get one ADDIU $7, $zero, 2 # register 7 should get 2 J num3
  //   #jumps to next line so delay slot should be executed twice num3: ADDIU $8, $zero, 7 #should happen
  //   twice once as delay slop then once jump so $8=14 SLL $0, $0, 0 J num4 #jumps to JAL test cases SLL
  //   $0, $0, 0 num1: ADDIU $3, $zero, 3 #$3 should be 3 J num2 #jumping "backwards" SLL $0, $0, 0 ADDIU
  //   $4, $zero, 5 #should be flushed ADDIU $5, $zero, 6 #should not be executed so $5 should stay 0
  //   #JAL Test Cases num4: JAL num5 #JALing forward SLL $0, $0, 0 ADDIU $1, $zero, 5 #should be flushed
  //   ADDIU $2, $zero, 6 #should not be executed so $2 should stay 0 num6: ADDIU $11, $zero, 1 # register
  //   11 should get one ADDIU $12, $zero, 2 # register 12 should get 2 JAL num7 #jumps to next line so
  //   delay slot should be executed twice num7: ADDIU $13, $zero, 10 #should happen twice once as delay
  //   slop then once jump so $13= 20 ############### SLL $0, $0, 0 JAL num8 # after this we are changing
  //   reg 31 so before this point we should check that reg 31 has the correct value. SLL $0, $0, 0 num5:
  //   ADDIU $9, $zero, 1 # register 9 should get one ADDIU $10, $zero, 2 # register 10 should get 2 JAL
  //   num6 #JALing "backward" SLL $0, $0, 0 num8: ADDIU $31, $zero, 5 #$31=5 JAL num9 SLL $0, $0, 0 SLL
  //   $0, $0, 0 num9: ADDIU $14, $31, 0 #14 should get value of regiser so much larget than 5. ADDIU $15,
  //   $zero, 24 JAL num10 SLL $0, $0, 0 num10: ADDIU $31, $zero ,3 #regiser 31 should have 3 and not
  //   register value J num11 SLL $0, $0, 0   #JR num11: ADDIU $15, $zero, 180 #$15 should get 180 JR $15 #
  //   ($15 prev value 180) SLL $0, $0, 0 ADDIU $16, $zero, 7 #$16 should get 7 because this is the
  //   instruction that we are jumping to ADDIU $17, $zero, 6 #$17 should get 6 ADDIU $18, $zero, 208 ADDIU
  //   $22, $zero, 2 JR $18 #should jump tp ADDIU $19 ADDIU $22, $zero, 5 #delay slot should be executed
  //   ADDIU $18, $zero, 6 #should be flushed, 18 should remain the same (204)  #JALR ADDIU $19, $zero, 240
  //   # value of rs should be forwarded to the JALR ADDIU $20, $zero,5 # should get 5 and then be
  //   immediately overritten by the JALR return address. JALR $20, $19 ADDIU $23, $zero, 3 #delay slot
  //   should be executed. SLL $0, $0, 0 J jalr1 ADDIU $23, $zero, 4 #will never be executed ADDIU $21,
  //   $zero, 10 #will never be executed JR $20 # should go to pc+8, so now $23 should get a value of 4.
  //   SLL $0, $0, 0 SLL $0, $0, 0 SLL $0, $0, 0 SLL $0, $0, 0 jalr1: ADDIU $7, $zero,276 #jumps to last
  //   SLL before BEQ JALR  $8, $7 SLL $0, $0, 0 JALR $3, $4 #should never be executed bc in pc +8 should
  //   be zapped SLL $0, $0, 0  #BEQ Test Cases ADDIU $24, $zero, 3 ADDIU $25, $zero, 3 ADDIU $29, $zero, 0
  //   ADDIU $30, $zero, 0 ADDIU $1, $zero, 5 ADDIU $2, $zero, 5 BEQ $24, $25, branch1 #branch should be
  //   taken bc the registers equal. ADDIU $5, $zero, 19 # $5=19, branch is taken but want to make sure
  //   that delay slot is executed ADDIU $24, $24, 0 # should not change bc branch was taken ADDIU $25,
  //   $25, 0 # should not change bc branch was taken branch3: ADDIU $3, $zero, 6 #$3 should equal 6 ADDIU
  //   $4, $zero, 7 #$4 should equal 7 J endBEQ SLL $0, $0, 0 branch1: ADDIU $26, $zero, 5 # $26=5 ADDIU
  //   $27, $zero, 6 #$27=6 BEQ $26, $27, branch2 #branch should not be taken SLL $0, $0, 0 ADDIU $28,
  //   $zero, 1 #$28 should equal one because branch was not taken. BEQ $1, $2, branch3 # branching
  //   backwards this is equvalent to a negative offset SLL $0, $0, 0 branch2: ADDIU $29, $zero, 1 #should
  //   not change beacuse branch was not taken prev value= 0 ADDIU $30, $zero, 1 #should not change beacuse
  //   branch was not taken prev value= 0 endBEQ: SLL $0, $0, 0 SLL $0, $0, 0 SLL $0, $0, 0 SLL $0, $0, 0
  //   #BNE Test Cases. ADDIU $6, $zero, 3 ADDIU $7, $zero, 3 ADDIU $8, $zero, 0 ADDIU $9, $zero, 0 ADDIU
  //   $10, $zero, 5 ADDIU $11, $zero, 5 BNE $6, $6, bne1 #branch should not be ta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
endmodule

module instructionDecode (
  input  [31:0] D,
  input  skip,
  input  clck,
  input  [31:0] inst,
  input  [31:0] PCPlus4,
  input  [4:0] rd,
  output [31:0] A,
  output [31:0] B,
  output [4:0] rdOut,
  output [4:0] Sa,
  output [31:0] imm,
  output SLTIU,
  output [3:0] ctrl,
  output SLTI,
  output I,
  output SLTU,
  output SLT,
  output skipOut,
  output LUI,
  output MOVN,
  output MOVZ,
  output [31:0] PCPlus4out,
  output [4:0] rtOut,
  output [4:0] rsOut,
  output shiftVar,
  output [31:0] indexJ,
  output [31:0] manipOff,
  output [2:0] JUMP,
  output [3:0] Branch,
  output LW,
  output LB,
  output LBU,
  output SW,
  output IDEXMEMR,
  output SB
);

  wire or_1_out;
  wire [4:0] decode_1_saout;

  decode decode_1 (
    .Instruction(inst), .SLTIU(SLTIU), .SLTI(SLTI), .I(I), .ctrl(ctrl), .Var(shiftVar),
    .SaOut(decode_1_saout), .SLTU(SLTU), .SLT(SLT), .skip(skipOut), .Imm(imm), .LUI(LUI), .MOVN(MOVN),
    .MOVZ(indexJ[1]), .JUMP(JUMP), .Branch(Branch), .LW(LW), .LB(LB), .LBU(LBU), .SW(SW), .SB(SB));
  assign manipOff[31:18] = {{13{inst[15]}}, inst[15]};  // Bit_Extender bit_extender_1
  // RegisterFile #(.trigger("falling")) registerfile_1: pin names not known; wires that end beside it: D, clck, skip, rd, inst[25:21], inst[20:16], A, B
  or or_1 (or_1_out, I, LUI);
  Multiplexer #(.width(5), .enable("false")) multiplexer_1 (
    .in0(inst[15:11]), .in1(inst[20:16]), .out(rdOut), .sel(or_1_out));
  Multiplexer #(.width(5), .enable("false")) multiplexer_2 (
    .in0(decode_1_saout), .in1(A[4:0]), .out(Sa), .sel(shiftVar));
  or or_2 (IDEXMEMR, LW, LB, LBU);

  assign {indexJ[31:2], indexJ[0]} = {PCPlus4[31:28], inst[25:0], indexJ[1]};
  assign manipOff[17:0] = {inst[15:0], {2{indexJ[1]}}};
  assign MOVZ = indexJ[1];
  assign PCPlus4out = PCPlus4;
  assign rsOut = inst[25:21];
  assign rtOut = inst[20:16];
endmodule

module decode (
  input  [31:0] Instruction,
  output SLTIU,
  output SLTI,
  output I,
  output [3:0] ctrl,
  output Var,
  output [4:0] SaOut,
  output SLTU,
  output SLT,
  output skip,
  output [31:0] Imm,
  output LUI,
  output MOVN,
  output MOVZ,
  output [2:0] JUMP,
  output [3:0] Branch,
  output LW,
  output LB,
  output LBU,
  output SW,
  output SB
);

  wire and_3_out, and_4_out, itype_1_lui, itype_1_slti, itype_1_sltiu, jbranchtype_1_skip,
       loadstoretype_1_wdis, not_1_out, not_2_out, not_3_out, not_4_out, not_5_out, or_1_out, or_2_out,
       or_3_out, or_4_out, or_7_out, or_8_out, rtype_1_jalr, rtype_1_jr, rtype_1_movn, rtype_1_movz,
       rtype_1_skip, rtype_1_slt, rtype_1_sltu;
  wire [1:0] jbranchtype_1_jl;
  wire [3:0] itype_1_ctrl, jbranchtype_1_ctrl, loadstoretype_1_ctrl, multiplexer_1_out, multiplexer_2_out,
       rtype_1_ctrl;

  LoadStoreType loadstoretype_1 (
    .Bit26to31(Instruction[31:26]), .Wdis(loadstoretype_1_wdis), .LW(LW), .LB(LB), .LBU(LBU), .SW(SW),
    .ctrl(loadstoretype_1_ctrl), .SB(SB));
  Rtype rtype_1 (
    .Sa(Instruction[10:6]), .func(Instruction[5:0]), .Var(Var), .SaOut(SaOut), .ctrl(rtype_1_ctrl),
    .SLT(rtype_1_slt), .Skip(rtype_1_skip), .MOVN(rtype_1_movn), .MOVZ(rtype_1_movz), .SLTU(rtype_1_sltu),
    .JR(rtype_1_jr), .JALR(rtype_1_jalr));
  JBranchType jbranchtype_1 (
    .Bit29(Instruction[29]), .bit26to28(Instruction[28:26]), .bit16to20(Instruction[20:16]),
    .Bit31(Instruction[31]), .skip(jbranchtype_1_skip), .JL(jbranchtype_1_jl), .Branch(Branch),
    .ctrl(jbranchtype_1_ctrl));
  Itype itype_1 (
    .imm0To15(Instruction[15:0]), .Opcode26To28(Instruction[28:26]), .SLTIU(itype_1_sltiu),
    .SLTI(itype_1_slti), .ctrl(itype_1_ctrl), .Imm(Imm), .LUI(itype_1_lui));
  or or_1 (or_1_out, loadstoretype_1_wdis, jbranchtype_1_skip);
  or or_2 (or_2_out, LW, LB, LBU);
  or or_3 (or_3_out, rtype_1_jalr, rtype_1_jr);
  Multiplexer #(.width(4), .enable("false")) multiplexer_1 (
    .in0(rtype_1_ctrl), .in1(itype_1_ctrl), .out(multiplexer_1_out), .sel(or_4_out));
  not not_1 (not_1_out, or_4_out);
  and and_1 (JUMP[0], not_1_out, or_3_out);
  or or_4 (or_4_out, Instruction[26], Instruction[27], Instruction[28], Instruction[29], Instruction[30], Instruction[31]);
  not not_2 (not_2_out, or_4_out);
  and and_2 (I, or_4_out, not_4_out);
  Multiplexer #(.width(4), .enable("false")) multiplexer_2 (
    .in0(multiplexer_1_out), .in1(jbranchtype_1_ctrl), .out(multiplexer_2_out), .sel(Branch[3]));
  not not_3 (not_3_out, or_4_out);
  and and_3 (and_3_out, or_4_out, or_1_out);
  and and_4 (and_4_out, not_2_out, rtype_1_skip);
  or or_5 (JUMP[1], jbranchtype_1_jl[0], rtype_1_jalr);
  or or_6 (JUMP[2], jbranchtype_1_jl[1], JUMP[0]);
  and and_5 (SLTIU, itype_1_sltiu, I);
  and and_6 (SLTI, I, itype_1_slti);
  and and_7 (SLTU, rtype_1_sltu, not_3_out);
  and and_8 (SLT, not_3_out, rtype_1_slt);
  not not_4 (not_4_out, or_7_out);
  or or_7 (or_7_out, and_3_out, and_4_out);
  not not_5 (not_5_out, or_2_out);
  and and_9 (MOVN, not_2_out, rtype_1_movn);
  and and_10 (MOVZ, not_2_out, rtype_1_movz);
  and and_11 (skip, or_7_out, not_5_out);
  and and_12 (LUI, I, itype_1_lui);
  Multiplexer #(.width(4), .enable("false")) multiplexer_3 (
    .in0(multiplexer_2_out), .in1(loadstoretype_1_ctrl), .out(ctrl), .sel(or_8_out));
  or or_8 (or_8_out, or_2_out, SB, SW);
endmodule

module Rtype (
  input  [4:0] Sa,
  input  [5:0] func,
  output Var,
  output [4:0] SaOut,
  output [3:0] ctrl,
  output SLT,
  output Skip,
  output MOVN,
  output MOVZ,
  output SLTU,
  output JR,
  output JALR
);

  wire and_3_out, and_5_out, not_1_out, not_2_out, not_3_out, not_4_out, not_5_out, or_1_out,
       rtype1ops_1_slt, rtype1ops_1_sltu, shift_1_var;
  wire [3:0] rtype1ops_1_ctrl, shift_1_ctrl;

  shift shift_1 (.func0to3(func[3:0]), .Sa(Sa), .Var(shift_1_var), .ctrl(shift_1_ctrl), .Saout(SaOut));
  Rtype1Ops rtype1ops_1 (.func0to3(func[3:0]), .SLTU(rtype1ops_1_sltu), .SLT(rtype1ops_1_slt), .ctrl(rtype1ops_1_ctrl));
  not not_1 (not_1_out, func[5]);
  Multiplexer #(.width(4), .enable("false")) multiplexer_1 (
    .in0(shift_1_ctrl), .in1(rtype1ops_1_ctrl), .out(ctrl), .sel(func[5]));
  not not_2 (not_2_out, func[1]);
  and and_1 (SLTU, func[5], rtype1ops_1_sltu);
  and and_2 (SLT, rtype1ops_1_slt, func[5]);
  not not_3 (not_3_out, func[0]);
  or or_1 (or_1_out, SLTU, SLT);
  not not_4 (not_4_out, or_1_out);
  and and_3 (and_3_out, not_4_out, func[3]);
  and and_4 (Var, not_1_out, shift_1_var);
  and and_5 (and_5_out, and_3_out, func[1]);
  and and_6 (Skip, and_3_out, not_2_out);
  not not_5 (not_5_out, func[0]);
  and and_7 (MOVN, func[0], and_5_out);
  and and_8 (MOVZ, and_5_out, not_3_out);
  and and_9 (JR, Skip, not_5_out);
  and and_10 (JALR, Skip, func[0]);
endmodule

module Itype (
  input  [15:0] imm0To15,
  input  [2:0] Opcode26To28,
  output SLTIU,
  output SLTI,
  output [3:0] ctrl,
  output [31:0] Imm,
  output LUI
);

  wire and_1_out, not_1_out, not_2_out, signextended_1_slt, zeroextended_1_lui;
  wire [3:0] signextended_1_ctrl, zeroextended_1_ctrl;
  wire [31:0] signextended_1_immsigned, zeroextended_1_immzero;

  SignExtended signextended_1 (
    .OpCode26To28(Opcode26To28), .imm0To15(imm0To15), .SLT(signextended_1_slt), .ctrl(signextended_1_ctrl),
    .immSigned(signextended_1_immsigned));
  ZeroExtended zeroextended_1 (
    .OpCode26To28(Opcode26To28), .imm0To15(imm0To15), .LUI(zeroextended_1_lui), .ctrl(zeroextended_1_ctrl),
    .immZero(zeroextended_1_immzero));
  not not_1 (not_1_out, Opcode26To28[2]);
  Multiplexer #(.width(4), .enable("false")) multiplexer_1 (
    .in0(signextended_1_ctrl), .in1(zeroextended_1_ctrl), .out(ctrl), .sel(Opcode26To28[2]));
  and and_1 (and_1_out, signextended_1_slt, not_1_out);
  and and_2 (LUI, Opcode26To28[2], zeroextended_1_lui);
  not not_2 (not_2_out, Opcode26To28[0]);
  Multiplexer #(.width(32), .enable("false")) multiplexer_2 (
    .in0(signextended_1_immsigned), .in1(zeroextended_1_immzero), .out(Imm), .sel(Opcode26To28[2]));
  and and_3 (SLTIU, Opcode26To28[0], and_1_out);
  and and_4 (SLTI, not_2_out, and_1_out);
endmodule

module shift (
  input  [3:0] func0to3,
  input  [4:0] Sa,
  output Var,
  output [3:0] ctrl,
  output [4:0] Saout
);

  wire [3:0] shiftsa_1_ctrl, shiftvariable_1_ctrl;

  shiftSa shiftsa_1 (.func0to3(func0to3), .Sa(Sa), .ctrl(shiftsa_1_ctrl), .Saout(Saout));
  shiftVariable shiftvariable_1 (.funct0to3(func0to3), .ctrl(shiftvariable_1_ctrl));
  Multiplexer #(.width(4), .enable("false")) multiplexer_1 (
    .in0(shiftsa_1_ctrl), .in1(shiftvariable_1_ctrl), .out(ctrl), .sel(func0to3[2]));

  assign Var = func0to3[2];
endmodule

module shiftVariable (
  input  [3:0] funct0to3,
  output [3:0] ctrl
);


  assign ctrl = {funct0to3[3], funct0to3[1], funct0to3[3], funct0to3[0]};
endmodule

module shiftSa (
  input  [3:0] func0to3,
  input  [4:0] Sa,
  output [3:0] ctrl,
  output [4:0] Saout
);


  assign ctrl = {func0to3[3], func0to3[1], func0to3[2], func0to3[0]};
  assign Saout = Sa;
endmodule

module Rtype1Ops (
  input  [3:0] func0to3,
  output SLTU,
  output SLT,
  output [3:0] ctrl
);

  wire not_1_out;

  and and_1 (SLTU, func0to3[0], func0to3[3]);
  not not_1 (not_1_out, func0to3[0]);
  and and_2 (SLT, not_1_out, func0to3[3]);

  assign ctrl = {func0to3[2:0], func0to3[3]};
endmodule

module SignExtended (
  input  [2:0] OpCode26To28,
  input  [15:0] imm0To15,
  output SLT,
  output [3:0] ctrl,
  output [31:0] immSigned
);

  assign immSigned[31:15] = {{16{imm0To15[15]}}, imm0To15[15]};  // Bit_Extender bit_extender_1

  assign ctrl = {OpCode26To28, OpCode26To28[2]};
  assign immSigned[14:0] = imm0To15[14:0];
  assign SLT = OpCode26To28[1];
endmodule

module ZeroExtended (
  input  [2:0] OpCode26To28,
  input  [15:0] imm0To15,
  output LUI,
  output [3:0] ctrl,
  output [31:0] immZero
);

  not not_1 (ctrl[0], OpCode26To28[2]);
  assign immZero[31:16] = {{15{ctrl[0]}}, ctrl[0]};  // Bit_Extender bit_extender_1
  and and_1 (LUI, OpCode26To28[1], OpCode26To28[0]);

  assign ctrl[3:1] = OpCode26To28;
  assign immZero[15:0] = imm0To15;
endmodule

module JBranchType (
  input  Bit29,
  input  [2:0] bit26to28,
  input  [4:0] bit16to20,
  input  Bit31,
  output skip,
  output [1:0] JL,
  output [3:0] Branch,
  output [3:0] ctrl
);

  wire and_2_out, and_3_out, and_6_out, not_1_out, not_4_out, not_5_out, not_6_out, or_1_out;

  not not_1 (not_1_out, bit26to28[2]);
  not not_2 (Branch[1], bit26to28[1]);
  not not_3 (skip, Bit29);
  xnor xnor_1 (Branch[2], bit26to28[1], bit26to28[2]);
  not not_4 (not_4_out, bit26to28[2]);
  or or_1 (or_1_out, bit26to28[0], bit26to28[1], bit26to28[2]);
  not not_5 (not_5_out, Bit31);
  and and_1 (ctrl[3], bit26to28[1], not_1_out);
  and and_2 (and_2_out, not_4_out, Branch[1]);
  Multiplexer #(.enable("false")) multiplexer_1 (
    .in0(bit26to28[0]), .in1(bit16to20[0]), .out(Branch[0]), .sel(and_2_out));
  and and_3 (and_3_out, skip, not_5_out);
  and and_4 (JL[0], bit26to28[0], ctrl[3]);
  not not_6 (not_6_out, ctrl[3]);
  and and_5 (JL[1], ctrl[3], skip, not_5_out);
  and and_6 (and_6_out, not_6_out, or_1_out);
  and and_7 (Branch[3], and_6_out, and_3_out);

  assign ctrl[2:0] = {ctrl[3], Branch[3], ctrl[3]};
endmodule

module LoadStoreType (
  input  [5:0] Bit26to31,
  output Wdis,
  output LW,
  output LB,
  output LBU,
  output SW,
  output [3:0] ctrl,
  output SB
);

  wire not_2_out, not_3_out, not_4_out, not_5_out, not_6_out, not_7_out, not_8_out;

  not not_1 (ctrl[3], Bit26to31[5]);
  not not_2 (not_2_out, Bit26to31[0]);
  not not_3 (not_3_out, Bit26to31[1]);
  not not_4 (not_4_out, Bit26to31[3]);
  not not_5 (not_5_out, Bit26to31[3]);
  not not_6 (not_6_out, Bit26to31[2]);
  and and_1 (LW, Bit26to31[0], Bit26to31[1], not_5_out, Bit26to31[5]);
  and and_2 (LB, not_2_out, not_3_out, not_4_out, not_6_out, Bit26to31[5]);
  not not_7 (not_7_out, Bit26to31[0]);
  not not_8 (not_8_out, Bit26to31[1]);
  and and_3 (Wdis, Bit26to31[3], Bit26to31[5]);
  and and_4 (LBU, Bit26to31[5], Bit26to31[2]);
  and and_5 (SW, Bit26to31[0], Wdis, Bit26to31[1]);
  and and_6 (SB, Wdis, not_7_out, not_8_out);

  assign ctrl[2:0] = {ctrl[3], Bit26to31[5], ctrl[3]};
endmodule

module InExecute (
  input  [31:0] A,
  input  [31:0] B,
  input  [4:0] Sa,
  input  [31:0] imm,
  input  SLTIU,
  input  [3:0] ctrl,
  input  SLTI,
  input  I,
  input  SLTU,
  input  SLT,
  input  skip,
  input  LUI,
  input  MOVN,
  input  MOVZ,
  input  [4:0] rd,
  input  shiftVar,
  input  [31:0] indexJ,
  input  [31:0] manipOff,
  input  [2:0] jump,
  input  [3:0] Branch,
  input  [31:0] PCPlus4,
  input  LW,
  input  LB,
  input  LBU,
  input  SW,
  input  [4:0] rt,
  input  SB,
  output [31:0] Aout,
  output [31:0] D,
  output Wdis,
  output [4:0] rdOut,
  output [31:0] TAddress,
  output zap,
  output [31:0] MEMAdr,
  output [31:0] rtVal,
  output LWOut,
  output LBOut,
  output LBUOut,
  output SWOut,
  output [4:0] rtOut,
  output SBOut,
  output LOAD
);

  wire and_1_out, and_2_out, and_3_out, and_4_out, and_5_out, and_6_out, and_7_out, and_8_out,
       comparator_1_eq, comparator_1_lt, comparator_2_lt, comparator_3_eq, comparator_3_gt, comparator_3_lt,
       multiplexer_11_out, not_1_out, not_2_out, not_3_out, not_4_out, not_5_out, or_1_out, or_2_out,
       or_3_out, or_4_out, or_5_out, or_6_out, or_8_out, or_9_out, xnor_1_out, xor_1_out, xor_2_out;
  wire [0:0] multiplexer_7_out;
  wire [4:0] bit_extender_3_out, mips_alu_1_p4;
  wire [31:0] bit_extender_1_out, bit_extender_2_out, mips_alu_1_p2, multiplexer_1_out, multiplexer_2_out,
       multiplexer_3_out, multiplexer_4_out, multiplexer_5_out, multiplexer_8_out, multiplexer_10_out,
       multiplexer_12_out, multiplexer_13_out, multiplexer_14_out;
  wire [31:2] incrementer_1_p2;

  or or_1 (or_1_out, SLTI, SLT);
  or or_2 (or_2_out, LW, LB, SB, LBU, SW);
  or or_3 (or_3_out, SLTIU, SLTU);
  or or_4 (or_4_out, MOVN, MOVZ);
  not not_1 (not_1_out, jump[0]);
  Multiplexer #(.width(32), .enable("false")) multiplexer_1 (
    .in0(A), .in1(manipOff), .out(multiplexer_1_out), .sel(Branch[3]));
  Multiplexer #(.width(32), .enable("false")) multiplexer_2 (.in0(B), .in1(imm), .out(multiplexer_2_out), .sel(I));
  or or_5 (or_5_out, or_3_out, or_1_out);
  assign bit_extender_1_out = {{31{LUI}}, LUI};  // Bit_Extender bit_extender_1
  and and_1 (and_1_out, I, not_2_out);
  not not_2 (not_2_out, or_4_out);
  and and_2 (and_2_out, jump[0], jump[1], jump[2]);
  // Incrementer #(.width(30)) incrementer_1: pin names not known; wires that end beside it: PCPlus4[31:2], incrementer_1_p2
  Multiplexer #(.width(32), .enable("false")) multiplexer_3 (
    .in0(multiplexer_2_out), .in1(PCPlus4), .out(multiplexer_3_out), .sel(Branch[3]));
  Multiplexer #(.width(32), .enable("false")) multiplexer_4 (
    .in0(A), .in1(bit_extender_1_out), .out(multiplexer_4_out), .sel(or_4_out));
  Multiplexer #(.width(32), .enable("false")) multiplexer_5 (
    .in0(B), .in1(imm), .out(multiplexer_5_out), .sel(and_1_out));
  and and_3 (and_3_out, not_1_out, jump[1], jump[2]);
  and and_4 (and_4_out, jump[1], jump[2]);
  // Mips_ALU mips_alu_1: pin names not known; wires that end beside it: multiplexer_1_out, mips_alu_1_p2, ctrl, mips_alu_1_p4, MEMAdr
  Multiplexer #(.width(32), .enable("false")) multiplexer_6 (
    .in0(multiplexer_3_out), .in1(bit_extender_2_out), .out(mips_alu_1_p2), .sel(or_2_out));
  assign bit_extender_2_out = {{16{imm[15]}}, imm[15:0]};  // Bit_Extender bit_extender_2
  Comparator #(.width(32)) comparator_1 (
    .a(multiplexer_4_out), .b(multiplexer_5_out), .eq(comparator_1_eq), .lt(comparator_1_lt));  // open: gt
  Comparator #(.width(32), .mode("unsigned")) comparator_2 (
    .a(A), .b(multiplexer_5_out), .lt(comparator_2_lt));  // open: gt, eq
  assign bit_extender_3_out = {{4{and_3_out}}, and_3_out};  // Bit_Extender bit_extender_3
  or or_6 (or_6_out, and_3_out, and_2_out);
  not not_3 (not_3_out, and_4_out);
  Multiplexer #(.enable("false")) multiplexer_7 (
    .in0(comparator_1_lt), .in1(comparator_2_lt), .out(multiplexer_7_out[0]), .sel(or_3_out));
  Multiplexer #(.width(32), .enable("false")) multiplexer_8 (
    .in0(B), .in1(bit_extender_1_out), .out(multiplexer_8_out), .sel(Branch[2]));
  Multiplexer #(.width(5), .enable("false")) multiplexer_9 (
    .in0(Sa), .in1(A[4:0]), .out(mips_alu_1_p4), .sel(shiftVar));
  Comparator #(.width(32)) comparator_3 (
    .a(A), .b(multiplexer_8_out), .gt(comparator_3_gt), .eq(comparator_3_eq), .lt(comparator_3_lt));
  not not_4 (not_4_out, comparator_1_eq);
  and and_5 (and_5_out, not_4_out, MOVN);
  and and_6 (and_6_out, MOVZ, comparator_1_eq);
  not not_5 (not_5_out, or_8_out);
  assign rdOut = rd | bit_extender_3_out;  // OR_Gate or_7, 5 bits wide
  xnor xnor_1 (xnor_1_out, comparator_3_gt, Branch[0]);
  xor xor_1 (xor_1_out, comparator_3_eq, Branch[0]);
  xor xor_2 (xor_2_out, comparator_3_lt, Branch[0]);
  Multiplexer #(.width(32), .enable("false")) multiplexer_10 (
    .in0(MEMAdr), .in1({bit_extender_1_out[31:1], multiplexer_7_out[0]}), .out(multiplexer_10_out),
    .sel(or_5_out));
  or or_8 (or_8_out, and_5_out, and_6_out);
  and and_7 (and_7_out, not_5_out, or_4_out);
  Multiplexer #(.select(2), .enable("false")) multiplexer_11 (
    .in0(LUI), .in1(xor_1_out), .in2(xnor_1_out), .in3(xor_2_out), .out(multiplexer_11_out), .sel(Branch[2:1]));
  or or_9 (or_9_out, and_7_out, skip);
  and and_8 (and_8_out, multiplexer_11_out, Branch[3]);
  Multiplexer #(.width(32), .enable("false")) multiplexer_12 (
    .in0(multiplexer_10_out), .in1({imm[15:0], imm[31:16]}), .out(multiplexer_12_out), .sel(LUI));
  Multiplexer #(.width(32), .enable("false")) multiplexer_13 (
    .in0(indexJ), .in1(A), .out(multiplexer_13_out), .sel(jump[0]));
  Multiplexer #(.width(32), .enable("false")) multiplexer_14 (
    .in0(multiplexer_12_out), .in1(A), .out(multiplexer_14_out), .sel(or_8_out));
  Multiplexer #(.width(32), .enable("false")) multiplexer_15 (
    .in0(multiplexer_13_out), .in1(MEMAdr), .out(TAddress), .sel(Branch[3]));
  Multiplexer #(.width(32), .enable("false")) multiplexer_16 (
    .in0(multiplexer_14_out), .in1({incrementer_1_p2, PCPlus4[1:0]}), .out(D), .sel(or_6_out));
  and and_9 (Wdis, or_9_out, not_3_out);
  or or_10 (zap, jump[2], and_8_out);
  or or_11 (LOAD, LW, LB, LBU);

  assign Aout = A;
  assign LBOut = LB;
  assign LBUOut = LBU;
  assign LWOut = LW;
  assign rtOut = rt;
  assign rtVal = B;
  assign SBOut = SB;
  assign SWOut = SW;
endmodule

module IDEX (
  input  [31:0] A,
  input  [31:0] B,
  input  [4:0] Sa,
  input  [31:0] imm,
  input  SLTIU,
  input  [3:0] ctrl,
  input  SLTI,
  input  I,
  input  clck,
  input  SLTU,
  input  SLT,
  input  Wdis,
  input  LUI,
  input  MOVN,
  input  MOVZ,
  input  [31:0] PCPlus4,
  input  [4:0] rd,
  input  [4:0] rt,
  input  [4:0] rs,
  input  shiftVar,
  input  [31:0] indexJ,
  input  [31:0] manipOff,
  input  [2:0] JUMP,
  input  [3:0] Branch,
  input  LW,
  input  LB,
  input  LBU,
  input  SW,
  input  IDEXMEMR,
  input  stall,
  input  SB,
  output [31:0] Aout,
  output [31:0] Bout,
  output [4:0] SaOut,
  output [31:0] immOut,
  output SLTIUout,
  output [3:0] ctrlOut,
  output SLTIout,
  output Iout,
  output SLTUout,
  output SLTout,
  output WdisOut,
  output LUIout,
  output MOVNout,
  output MOVZout,
  output [4:0] rdOut,
  output [4:0] rtOut,
  output [4:0] rsOut,
  output SVarOut,
  output [31:0] inJOut,
  output [31:0] offOut,
  output [2:0] Jout,
  output [3:0] branOut,
  output [31:0] plus4out,
  output LWOut,
  output LBOut,
  output LBUOut,
  output SWOut,
  output IDEXMRO,
  output SBOut
);

  wire and_2_out, and_4_out, and_5_out, and_6_out, and_7_out, and_8_out, and_10_out, and_11_out, and_12_out,
       and_15_out, and_16_out, and_20_out, and_21_out, and_22_out, not_1_out;
  wire [2:2] and_13_out;
  wire [3:0] and_3_out, bit_extender_2_out;
  wire [3:3] and_14_out;
  wire [4:0] and_1_out, and_17_out, and_18_out, and_19_out, bit_extender_1_out;
  wire [31:0] and_9_out, bit_extender_3_out;

  not not_1 (not_1_out, stall);
  assign bit_extender_1_out = {{4{not_1_out}}, not_1_out};  // Bit_Extender bit_extender_1
  assign bit_extender_2_out = {{3{not_1_out}}, not_1_out};  // Bit_Extender bit_extender_2
  Register #(.width(32)) register_1 (.D(A), .clk(clck), .Q(Aout));  // open: en, clr
  Register #(.width(32)) register_2 (.D(imm), .clk(clck), .Q(immOut));  // open: en, clr
  Register #(.width(1)) register_3 (.D(Wdis), .clk(clck), .Q(WdisOut));  // open: en, clr
  Register #(.width(32)) register_4 (.D(PCPlus4), .clk(clck), .Q(plus4out));  // open: en, clr
  assign bit_extender_3_out = {{31{not_1_out}}, not_1_out};  // Bit_Extender bit_extender_3
  assign and_1_out = bit_extender_1_out & Sa;  // AND_Gate and_1, 5 bits wide
  and and_2 (and_2_out, not_1_out, SLTIU);
  assign and_3_out = ctrl & bit_extender_2_out;  // AND_Gate and_3, 4 bits wide
  and and_4 (and_4_out, SLTI, not_1_out);
  and and_5 (and_5_out, I, not_1_out);
  and and_6 (and_6_out, SLTU, not_1_out);
  and and_7 (and_7_out, SLT, not_1_out);
  and and_8 (and_8_out, shiftVar, not_1_out);
  Register #(.width(32)) register_5 (.D(indexJ), .clk(clck), .Q(inJOut));  // open: en, clr
  Register #(.width(32)) register_6 (.D(manipOff), .clk(clck), .Q(offOut));  // open: en, clr
  Register #(.width(1)) register_7 (.D(IDEXMEMR), .clk(clck), .Q(IDEXMRO));  // open: en, clr
  Register #(.width(32)) register_8 (.D(and_9_out), .clk(clck), .Q(Bout));  // open: en, clr
  assign and_9_out = bit_extender_3_out & B;  // AND_Gate and_9, 32 bits wide
  Register #(.width(5)) register_9 (.D(and_1_out), .clk(clck), .Q(SaOut));  // open: en, clr
  Register #(.width(1)) register_10 (.D(and_2_out), .clk(clck), .Q(SLTIUout));  // open: en, clr
  Register #(.width(1)) register_11 (.D(and_4_out), .clk(clck), .Q(SLTIout));  // open: en, clr
  Register #(.width(1)) register_12 (.D(and_5_out), .clk(clck), .Q(Iout));  // open: en, clr
  Register #(.width(1)) register_13 (.D(and_6_out), .clk(clck), .Q(SLTUout));  // open: en, clr
  Register #(.width(1)) register_14 (.D(and_7_out), .clk(clck), .Q(SLTout));  // open: en, clr
  and and_10 (and_10_out, LUI, not_1_out);
  and and_11 (and_11_out, MOVN, not_1_out);
  and and_12 (and_12_out, MOVZ, not_1_out);
  Register #(.width(1)) register_15 (.D(and_8_out), .clk(clck), .Q(SVarOut));  // open: en, clr
  and and_13 (and_13_out[2], JUMP[2], not_1_out);
  and and_14 (and_14_out[3], Branch[3], not_1_out);
  and and_15 (and_15_out, LW, not_1_out);
  and and_16 (and_16_out, LB, not_1_out);
  Register #(.width(4)) register_16 (.D(and_3_out), .clk(clck), .Q(ctrlOut));  // open: en, clr
  Register #(.width(1)) register_17 (.D(and_10_out), .clk(clck), .Q(LUIout));  // open: en, clr
  Register #(.width(1)) register_18 (.D(and_11_out), .clk(clck), .Q(MOVNout));  // open: en, clr
  Register #(.width(1)) register_19 (.D(and_12_out), .clk(clck), .Q(MOVZout));  // open: en, clr
  assign and_17_out = rd & bit_extender_1_out;  // AND_Gate and_17, 5 bits wide
  assign and_18_out = bit_extender_1_out & rt;  // AND_Gate and_18, 5 bits wide
  assign and_19_out = rs & bit_extender_1_out;  // AND_Gate and_19, 5 bits wide
  Register #(.width(3)) register_20 (.D({and_13_out[2], JUMP[1:0]}), .clk(clck), .Q(Jout));  // open: en, clr
  and and_20 (and_20_out, LBU, not_1_out);
  and and_21 (and_21_out, SW, not_1_out);
  and and_22 (and_22_out, SB, not_1_out);
  Register #(.width(5)) register_21 (.D(and_17_out), .clk(clck), .Q(rdOut));  // open: en, clr
  Register #(.width(5)) register_22 (.D(and_18_out), .clk(clck), .Q(rtOut));  // open: en, clr
  Register #(.width(5)) register_23 (.D(and_19_out), .clk(clck), .Q(rsOut));  // open: en, clr
  Register #(.width(4)) register_24 (.D({and_14_out[3], Branch[2:0]}), .clk(clck), .Q(branOut));  // open: en, clr
  Register #(.width(1)) register_25 (.D(and_15_out), .clk(clck), .Q(LWOut));  // open: en, clr
  Register #(.width(1)) register_26 (.D(and_16_out), .clk(clck), .Q(LBOut));  // open: en, clr
  Register #(.width(1)) register_27 (.D(and_20_out), .clk(clck), .Q(LBUOut));  // open: en, clr
  Register #(.width(1)) register_28 (.D(and_21_out), .clk(clck), .Q(SWOut));  // open: en, clr
  Register #(.width(1)) register_29 (.D(and_22_out), .clk(clck), .Q(SBOut));  // open: en, clr
endmodule

module IFID (
  input  [31:0] inst,
  input  [31:0] PCPlus4,
  input  clck,
  input  [4:0] IFrt,
  input  [4:0] IFrs,
  input  Stall,
  output [31:0] instOut,
  output [31:0] PCPlus4Out,
  output [4:0] IFIDrt,
  output [4:0] IFIDrs
);

  wire not_1_out;

  not not_1 (not_1_out, Stall);
  Register #(.width(32)) register_1 (.D(inst), .en(not_1_out), .clk(clck), .Q(instOut));  // open: clr
  Register #(.width(32)) register_2 (.D(PCPlus4), .en(not_1_out), .clk(clck), .Q(PCPlus4Out));  // open: clr
  Register #(.width(5)) register_3 (.D(IFrt), .en(not_1_out), .clk(clck), .Q(IFIDrt));  // open: clr
  Register #(.width(5)) register_4 (.D(IFrs), .en(not_1_out), .clk(clck), .Q(IFIDrs));  // open: clr
endmodule

module inMemory (
  input  [31:0] A,
  input  [31:0] D,
  input  skip,
  input  [4:0] rd,
  input  [31:0] MemAdr,
  input  [31:0] rtVal,
  input  LW,
  input  LB,
  input  LBU,
  input  SW,
  input  [4:0] rt,
  input  clck,
  input  SB,
  output [31:0] Aout,
  output [31:0] Dout,
  output Wdis,
  output [4:0] Wdest
);

  wire or_1_out, or_2_out, or_4_out;
  wire [1:0] or_6_out;
  wire [3:0] bit_extender_2_out, decoder_1_out0, or_3_out;
  wire [23:0] bit_extender_1_out;
  wire [31:0] bit_extender_3_out, bit_extender_4_out, bit_extender_5_out, bit_extender_6_out,
       bit_extender_7_out, bit_extender_8_out, bit_extender_9_out, bit_extender_10_out, mips_ram_1_p7,
       multiplexer_1_out, multiplexer_2_out, multiplexer_3_out;

  assign bit_extender_1_out = {{23{1'b0}}, LW};  // Bit_Extender bit_extender_1
  or or_1 (or_1_out, LW, LB, LBU);
  Multiplexer #(.select(2), .width(32), .enable("false")) multiplexer_1 (
    .in0({bit_extender_1_out, rtVal[7:0]}),
    .in1({bit_extender_1_out[23:8], rtVal[7:0], bit_extender_1_out[7:0]}),
    .in2({bit_extender_1_out[23:16], rtVal[7:0], bit_extender_1_out[15:0]}),
    .in3({rtVal[7:0], bit_extender_1_out}), .out(multiplexer_1_out), .sel(MemAdr[1:0]));
  or or_2 (or_2_out, LW, SW);
  assign bit_extender_2_out = {{3{or_2_out}}, or_2_out};  // Bit_Extender bit_extender_2
  Decoder #(.select(2), .enable("false")) decoder_1 (
    .out0(decoder_1_out0[0]), .out1(decoder_1_out0[1]), .out2(decoder_1_out0[2]), .out3(decoder_1_out0[3]),
    .sel(MemAdr[1:0]));
  assign or_3_out = decoder_1_out0 | bit_extender_2_out;  // OR_Gate or_3, 4 bits wide
  or or_4 (or_4_out, SB, SW);
  // MIPS_RAM mips_ram_1: pin names not known; wires that end beside it: MemAdr[21:2], multiplexer_1_out, or_4_out, or_3_out, clck, or_1_out, mips_ram_1_p7, mips_ram_1_p7[31:24]
  assign bit_extender_3_out = {{24{mips_ram_1_p7[7]}}, mips_ram_1_p7[7:0]};  // Bit_Extender bit_extender_3
  assign bit_extender_4_out = {{24{mips_ram_1_p7[15]}}, mips_ram_1_p7[15:8]};  // Bit_Extender bit_extender_4
  assign bit_extender_5_out = {{24{mips_ram_1_p7[23]}}, mips_ram_1_p7[23:16]};  // Bit_Extender bit_extender_5
  assign bit_extender_6_out = {{24{mips_ram_1_p7[31]}}, mips_ram_1_p7[31:24]};  // Bit_Extender bit_extender_6
  assign bit_extender_7_out = {{24{1'b0}}, mips_ram_1_p7[7:0]};  // Bit_Extender bit_extender_7
  assign bit_extender_8_out = {{24{1'b0}}, mips_ram_1_p7[15:8]};  // Bit_Extender bit_extender_8
  assign bit_extender_9_out = {{24{1'b0}}, mips_ram_1_p7[23:16]};  // Bit_Extender bit_extender_9
  assign bit_extender_10_out = {{24{1'b0}}, mips_ram_1_p7[31:24]};  // Bit_Extender bit_extender_10
  Multiplexer #(.select(2), .width(32), .enable("false")) multiplexer_2 (
    .in0(bit_extender_3_out), .in1(bit_extender_4_out), .in2(bit_extender_5_out), .in3(bit_extender_6_out),
    .out(multiplexer_2_out), .sel(MemAdr[1:0]));
  Multiplexer #(.select(2), .width(32), .enable("false")) multiplexer_3 (
    .in0(bit_extender_7_out), .in1(bit_extender_8_out), .in2(bit_extender_9_out), .in3(bit_extender_10_out),
    .out(multiplexer_3_out), .sel(MemAdr[1:0]));
  or or_5 (or_6_out[1], LBU, LW);
  or or_6 (or_6_out[0], LBU, LB);
  Multiplexer #(.select(2), .width(32), .enable("false")) multiplexer_4 (
    .in0(D), .in1(multiplexer_2_out), .in2(mips_ram_1_p7), .in3(multiplexer_3_out), .out(Dout), .sel(or_6_out));
  Multiplexer #(.width(5), .enable("false")) multiplexer_5 (.in0(rd), .in1(rt), .out(Wdest), .sel(or_1_out));
  or or_7 (Wdis, skip, SB, SW);

  assign Aout = A;
endmodule

module instrcutionWriteback (
  input  [31:0] D,
  input  [4:0] rd,
  input  skip,
  output [31:0] result,
  output [4:0] rdOut,
  output WE
);

  not not_1 (WE, skip);

  assign rdOut = rd;
  assign result = D;
endmodule

module EXMEM (
  input  [31:0] A,
  input  [31:0] D,
  input  clck,
  input  skip,
  input  [4:0] rd,
  input  [31:0] MemAdr,
  input  [31:0] rtVal,
  input  LW,
  input  LB,
  input  LBU,
  input  Sw,
  input  [4:0] rt,
  input  SB,
  output [31:0] Aout,
  output [31:0] Dout,
  output skipOut,
  output [4:0] rdOut,
  output [31:0] AdrOut,
  output [31:0] rtVOut,
  output LWOut,
  output LBOut,
  output LBUOut,
  output SWOut,
  output [4:0] rtOut,
  output SBOut
);

  Register #(.width(32)) register_1 (.D(A), .clk(clck), .Q(Aout));  // open: en, clr
  Register #(.width(32)) register_2 (.D(D), .clk(clck), .Q(Dout));  // open: en, clr
  Register #(.width(1)) register_3 (.D(skip), .clk(clck), .Q(skipOut));  // open: en, clr
  Register #(.width(5)) register_4 (.D(rd), .clk(clck), .Q(rdOut));  // open: en, clr
  Register #(.width(32)) register_5 (.D(MemAdr), .clk(clck), .Q(AdrOut));  // open: en, clr
  Register #(.width(32)) register_6 (.D(rtVal), .clk(clck), .Q(rtVOut));  // open: en, clr
  Register #(.width(1)) register_7 (.D(LW), .clk(clck), .Q(LWOut));  // open: en, clr
  Register #(.width(1)) register_8 (.D(LB), .clk(clck), .Q(LBOut));  // open: en, clr
  Register #(.width(1)) register_9 (.D(LBU), .clk(clck), .Q(LBUOut));  // open: en, clr
  Register #(.width(1)) register_10 (.D(Sw), .clk(clck), .Q(SWOut));  // open: en, clr
  Register #(.width(5)) register_11 (.D(rt), .clk(clck), .Q(rtOut));  // open: en, clr
  Register #(.width(1)) register_12 (.D(SB), .clk(clck), .Q(SBOut));  // open: en, clr
endmodule

module MEMWB (
  input  [31:0] A,
  input  [31:0] D,
  input  clck,
  input  skip,
  input  [4:0] rd,
  output [31:0] Dout,
  output skipOut,
  output [4:0] rdOut
);

  Register #(.width(32)) register_1 (.D(A), .clk(clck));  // open: en, Q, clr
  Register #(.width(32)) register_2 (.D(D), .clk(clck), .Q(Dout));  // open: en, clr
  Register #(.width(1)) register_3 (.D(skip), .clk(clck), .Q(skipOut));  // open: en, clr
  Register #(.width(5)) register_4 (.D(rd), .clk(clck), .Q(rdOut));  // open: en, clr
endmodule

module Hazards (
  input  [4:0] IDEXrt,
  input  [4:0] IDEXrs,
  input  [4:0] EXMEMrd,
  input  EXMEMregWrite,
  input  [4:0] MEMWBrd,
  input  MEMWBregWrite,
  input  IDEXMemread,
  input  [4:0] IFIDrs,
  input  [4:0] IFIDrt,
  input  LOAD,
  output [1:0] HazardA,
  output [1:0] HazardB,
  output Stall
);

  wire and_1_out, and_2_out, and_3_out, and_4_out, and_5_out, and_6_out, and_7_out, and_8_out, and_13_out,
       neq_1_o, neq_2_o, or_1_out;
  wire [4:0] xnor_1_out, xnor_2_out, xnor_3_out, xnor_4_out, xnor_5_out, xnor_6_out;

  neq neq_1 (.i(EXMEMrd), .O(neq_1_o));
  assign xnor_1_out = ~(IDEXrs ^ MEMWBrd);  // XNOR_Gate xnor_1, 5 bits wide
  assign xnor_2_out = ~(IDEXrt ^ MEMWBrd);  // XNOR_Gate xnor_2, 5 bits wide
  assign xnor_3_out = ~(IDEXrt ^ EXMEMrd);  // XNOR_Gate xnor_3, 5 bits wide
  assign xnor_4_out = ~(IDEXrs ^ EXMEMrd);  // XNOR_Gate xnor_4, 5 bits wide
  and and_1 (and_1_out, neq_1_o, EXMEMregWrite);
  neq neq_2 (.i(MEMWBrd), .O(neq_2_o));
  assign xnor_5_out = ~(IFIDrs ^ IDEXrt);  // XNOR_Gate xnor_5, 5 bits wide
  assign xnor_6_out = ~(IDEXrt ^ IFIDrt);  // XNOR_Gate xnor_6, 5 bits wide
  and and_2 (and_2_out, xnor_3_out[0], xnor_3_out[1], xnor_3_out[2], xnor_3_out[3], xnor_3_out[4]);
  and and_3 (and_3_out, MEMWBregWrite, neq_2_o);
  and and_4 (and_4_out, xnor_1_out[0], xnor_1_out[1], xnor_1_out[2], xnor_1_out[3], xnor_1_out[4]);
  and and_5 (and_5_out, xnor_2_out[0], xnor_2_out[1], xnor_2_out[2], xnor_2_out[3], xnor_2_out[4]);
  and and_6 (and_6_out, xnor_5_out[0], xnor_5_out[1], xnor_5_out[2], xnor_5_out[3], xnor_5_out[4]);
  and and_7 (and_7_out, xnor_6_out[0], xnor_6_out[1], xnor_6_out[2], xnor_6_out[3], xnor_6_out[4]);
  and and_8 (and_8_out, xnor_4_out[0], xnor_4_out[1], xnor_4_out[2], xnor_4_out[3], xnor_4_out[4]);
  and and_9 (HazardA[1], and_8_out, and_1_out);
  or or_1 (or_1_out, and_6_out, and_7_out);
  and and_10 (HazardB[1], and_2_out, and_1_out);
  and and_11 (HazardA[0], and_4_out, and_3_out);
  and and_12 (HazardB[0], and_3_out, and_5_out);
  and and_13 (and_13_out, IDEXMemread, or_1_out);
  and and_14 (Stall, and_13_out, LOAD);
endmodule

module neq (
  input  [4:0] i,
  output O
);

  or or_1 (O, i[0], i[1], i[2], i[3], i[4]);
endmodule
